// Logisim project 黄浩链MIPS32CPU.circ as structural Verilog: 5 circuits, main circuit main
module main (
  input  in_1,
  input  reset,
  input  EN
);

  wire ALU_X_Sel, ALU_X_sel_t, D_SELECT, F_IN_SEL, OF, R_MEM_HUANG021, RAM_Addr_s_HUANG021, S_Extend, SF,
       SKIP_HUANG021, undriven, undriven_2, undriven_3, undriven_4, undriven_5, undriven_6, undriven_8,
       W_F_HUANG021, W_GR_HUANG021, W_IR, W_IR_HUANG021, W_MEM_HUANG021, W_PC_HUANG021, W_RAM, W_RF_GR, ZF,
       \指令译码逻辑_黄浩链021_1_add , \指令译码逻辑_黄浩链021_1_addi , \指令译码逻辑_黄浩链021_1_beq , \指令译码逻辑_黄浩链021_1_sw ;
  wire [1:0] ALU_Y_Sel, GR_D_S, rd_rt_sel_HUANG021;
  wire [2:0] PC_D_Sel_HUANG021;
  wire [3:0] ALU_OP;
  wire [4:0] multiplexer_2_out;
  wire [5:0] funct, OP;
  wire [15:6] Imm;
  wire [23:10] cu_huang021_1_out_7;
  wire [27:0] PC_4;
  wire [31:0] A, \A_黄浩链_q , B, \B_黄浩链_q , demultiplexer_1_out0, demultiplexer_1_out1, F_HUANG, main_1_q1,
       main_1_q2, MDR, multiplexer_1_out, multiplexer_3_out, multiplexer_4_out, multiplexer_7_out,
       \n32位扩展器黄浩链_1_out_3 , PC, PC_8, \RAM_黄浩链_data , shifter_1_out, undriven_7;
  wire [31:18] J_PC;

  Multiplexer #(.select(3), .width(32), .disabled("Z"), .enable("false")) multiplexer_1 (
    .in0({J_PC[31:28], PC_4}), .in3(F_HUANG), .in4({J_PC, Imm, funct, 2'b00}),
    .in5({J_PC, Imm, funct, 2'b00}), .in6(A), .out(multiplexer_1_out), .sel(PC_D_Sel_HUANG021));  // open: in1, in2, in7
  Register #(.width(32), .trigger("falling"), .Select("high")) \PC_黄浩链  (
    .D(multiplexer_1_out), .en(W_PC_HUANG021), .Q(PC), .clk(undriven));  // open: clr
  Multiplexer #(.select(2), .width(5), .disabled("Z"), .enable("false")) multiplexer_2 (
    .in1(J_PC[22:18]), .in2({5{1'b1}}), .in3(Imm[15:11]), .out(multiplexer_2_out), .sel(rd_rt_sel_HUANG021));  // open: in0
  Multiplexer #(.select(1), .width(32), .disabled("Z"), .enable("false")) multiplexer_3 (
    .in0(PC), .in1(F_HUANG), .out(multiplexer_3_out), .sel(RAM_Addr_s_HUANG021));
  CU_HUANG021 cu_huang021_1 (
    .in_1(ZF), .in_2(OF),
    .out_7({cu_huang021_1_out_7, SKIP_HUANG021, W_GR_HUANG021, W_PC_HUANG021, W_F_HUANG021, S_Extend, ALU_X_sel_t, W_IR_HUANG021, R_MEM_HUANG021, W_MEM_HUANG021, RAM_Addr_s_HUANG021}),
    .rd_rt_sel(rd_rt_sel_HUANG021), .ALU_Y_sel(ALU_Y_Sel), .GR_D_sel(GR_D_S), .PC_D_SEL(PC_D_Sel_HUANG021),
    .ALU_OP(ALU_OP), .in_3(EN), .in_4(in_1), .in_5(OP), .in_6(funct));
  RF_32_main main_1 (
    .N1(J_PC[27:23]), .N2(J_PC[22:18]), .ND(multiplexer_2_out), .D_in(multiplexer_4_out), .WRITEREG(W_RF_GR),
    .CLK(undriven_2), .Q1(main_1_q1), .Q2(main_1_q2));  // open: RESET
  Multiplexer #(.select(2), .width(32), .disabled("Z"), .enable("false")) multiplexer_4 (
    .in0(F_HUANG), .in1(32'h1), .in2({32{1'b0}}), .in3(MDR), .out(multiplexer_4_out), .sel(GR_D_S));
  \时序发生器_7状态_main  main_2 (
    .En(EN), .skip(SKIP_HUANG021), .clk(in_1), .clr(reset));  // open: M0, M1, M2, M7, M6, M5, M4, M3
  Register #(.width(32), .trigger("rising"), .Select("high")) \A_黄浩链  (
    .D(main_1_q1), .en(1'b1), .Q(\A_黄浩链_q ), .clk(undriven_3));  // open: clr
  Register #(.width(32), .trigger("rising"), .Select("low")) \B_黄浩链  (
    .D(main_1_q2), .en(1'b1), .Q(\B_黄浩链_q ), .clk(undriven_4));  // open: clr
  RAM #(.addrWidth(8), .dataWidth(32), .bus("separate"), .Select("high")) \RAM_黄浩链  (
    .addr(multiplexer_3_out[7:0]), .din(B), .data(\RAM_黄浩链_data ), .str(W_RAM), .ld(R_MEM_HUANG021));  // open: sel, clk, clr
  \_32位扩展器黄浩链  \u_32位扩展器黄浩链_1  (.D_lin({Imm, funct}), .out_3(\n32位扩展器黄浩链_1_out_3 ));  // open: D_sel_Huang
  Multiplexer #(.select(1), .width(32), .disabled("Z"), .enable("false")) multiplexer_5 (
    .in0(PC), .in1(\A_黄浩链_q ), .out(A), .sel(ALU_X_Sel));
  Shifter #(.width(32), .shift("ll")) shifter_1 (.in(\n32位扩展器黄浩链_1_out_3 ), .\dist (5'b00010), .out(shifter_1_out));
  Demultiplexer #(.select(1), .width(32), .tristate("false"), .disabled("Z"), .enable("false")) demultiplexer_1 (
    .out0(demultiplexer_1_out0), .out1(demultiplexer_1_out1), .in(\RAM_黄浩链_data ), .sel(D_SELECT));
  Multiplexer #(.select(2), .width(32), .disabled("Z"), .enable("false")) multiplexer_6 (
    .in0(32'h4), .in1(\B_黄浩链_q ), .in2(\n32位扩展器黄浩链_1_out_3 ), .in3(shifter_1_out), .out(B), .sel(ALU_Y_Sel));
  \指令译码逻辑_黄浩链021  \u_指令译码逻辑_黄浩链021_1  (
    .OP(OP), .Funct(funct), .ADD(\指令译码逻辑_黄浩链021_1_add ), .SW(\指令译码逻辑_黄浩链021_1_sw ),
    .BEQ(\指令译码逻辑_黄浩链021_1_beq ), .ADDI(\指令译码逻辑_黄浩链021_1_addi ));
  Register #(.width(32), .trigger("falling"), .Select("low")) \MDR_黄浩链  (
    .D(demultiplexer_1_out0), .en(W_IR), .Q(MDR), .clk(undriven_5));  // open: clr
  Register #(.width(32), .trigger("falling"), .Select("low")) \IR_黄浩链  (
    .D(demultiplexer_1_out1), .en(W_IR_HUANG021), .Q({OP, J_PC[27:18], Imm, funct}), .clk(undriven_6));  // open: clr
  \黄浩链20212132021ALU  \u_黄浩链20212132021alu_1  (
    .in_1(A), .in_2(B), .\移位位数sa (Imm[10:6]), .F({J_PC[31:28], PC_4}), .ALU_OP_021(ALU_OP), .OF(OF), .SF(SF),
    .ZF(ZF));
  Adder #(.width(32)) adder_1 (.a({J_PC[31:28], PC_4}), .b(undriven_7), .out(PC_8));  // open: cin, cout
  Multiplexer #(.select(1), .width(32), .disabled("Z"), .enable("false")) multiplexer_7 (
    .in0({J_PC[31:28], PC_4}), .in1(PC_8), .out(multiplexer_7_out), .sel(F_IN_SEL));
  Register #(.width(32), .trigger("rising"), .Select("low")) \F_黄浩链  (
    .D(multiplexer_7_out), .en(1'b1), .Q(F_HUANG), .clk(undriven_8));  // open: clr

  // Other names for the same wires on the sheet: Imm[5:0] = funct; J_PC[17:2] = {Imm, funct};
  //   JAL_PC[31:2] = {J_PC, Imm, funct}; Target[25:0] = {J_PC[27:18], Imm, funct}; Sa[4:0] = Imm[10:6];
  //   rd[4:0] = Imm[15:11]; rt[4:0] = J_PC[22:18]; rs[4:0] = J_PC[27:23]; PC_4[31:28] = J_PC[31:28]
endmodule

module \黄浩链20212132021ALU  (
  input  [31:0] in_1,
  input  [31:0] in_2,
  input  [3:0] ALU_OP_021,
  input  [4:0] \移位位数sa ,
  output [31:0] F,
  output OF,
  output SF,
  output ZF
);

  wire adder_2_cout, adder_3_cout, adder_4_cout, adder_5_cout, \S有符号减溢出 , \S有符号加溢出 ;
  wire [31:0] not_1_out, \S与运算 , \S异或运算 , \S或运算 , \S无符号减 , \S无符号加 , \S有符号减 , \S有符号加 , \S算术右移 , \S逻辑右移 ,
       \S逻辑左移 ;

  // Probe on in_1
  // Probe on in_2
  assign not_1_out = ~in_2;  // NOT_Gate not_1, 32 bits wide
  Adder #(.width(32)) adder_1 (.a(in_1), .b(in_2), .out(\S无符号加 ), .cin(1'b0));  // open: cout
  Subtractor #(.width(32)) subtractor_1 (.a(in_1), .b(in_2), .out(\S无符号减 ), .bin(1'b0));  // open: bout
  Adder #(.width(31)) adder_2 (.a(in_1[30:0]), .b(in_2[30:0]), .out(\S有符号加 [30:0]), .cin(1'b0), .cout(adder_2_cout));
  Adder #(.width(1)) adder_3 (.a(in_1[31]), .b(in_2[31]), .out(\S有符号加 [31]), .cin(adder_2_cout), .cout(adder_3_cout));
  Comparator #(.width(32), .mode("twosComplement")) comparator_1 (.a(in_1), .b(in_2), .lt(SF));  // open: gt, eq
  assign \S与运算  = in_1 & in_2;  // AND_Gate and_1, 32 bits wide
  assign \S或运算  = in_1 | in_2;  // OR_Gate or_1, 32 bits wide
  assign \S异或运算  = in_1 ^ in_2;  // XOR_Gate xor_1, 32 bits wide
  Shifter #(.width(32), .shift("ll")) shifter_1 (.in(in_2), .\dist (\移位位数sa ), .out(\S逻辑左移 ));
  Shifter #(.width(32), .shift("lr")) shifter_2 (.in(in_2), .\dist (\移位位数sa ), .out(\S逻辑右移 ));
  Shifter #(.width(32), .shift("ar")) shifter_3 (.in(in_2), .\dist (\移位位数sa ), .out(\S算术右移 ));
  Adder #(.width(31)) adder_4 (
    .a(in_1[30:0]), .b(not_1_out[30:0]), .out(\S有符号减 [30:0]), .cin(1'b1), .cout(adder_4_cout));
  Adder #(.width(1)) adder_5 (
    .a(in_1[31]), .b(not_1_out[31]), .out(\S有符号减 [31]), .cin(adder_4_cout), .cout(adder_5_cout));
  xor xor_2 (\S有符号加溢出 , adder_2_cout, adder_3_cout);
  xor xor_3 (\S有符号减溢出 , adder_4_cout, adder_5_cout);
  nor nor_1 (ZF, F[31], F[30], F[29], F[28], F[27], F[26], F[25], F[24], F[23], F[22], F[21], F[20], F[19], F[18], F[17], F[16], F[15], F[14], F[13], F[12], F[11], F[10], F[9], F[8], F[7], F[6], F[5], F[4], F[3], F[2], F[1], F[0]);
  Multiplexer #(.select(4), .width(32), .disabled("Z"), .enable("false")) multiplexer_1 (
    .in0({32{1'b0}}), .in1(\S有符号加 ), .in2(\S无符号加 ), .in3(\S有符号减 ), .in4(\S无符号减 ), .in5(\S与运算 ), .in6(\S或运算 ),
    .in7(\S异或运算 ), .in8({32{1'b0}}), .in9(\S逻辑左移 ), .in10(\S逻辑右移 ), .in11(\S算术右移 ), .in12({32{1'b0}}),
    .in13({32{1'b0}}), .in14({32{1'b0}}), .in15({32{1'b0}}), .out(F), .sel(ALU_OP_021));
  Multiplexer #(.select(4), .width(1), .disabled("Z"), .enable("false")) multiplexer_2 (
    .in0(1'b0), .in1(\S有符号加溢出 ), .in2(1'b0), .in3(\S有符号减溢出 ), .in4(1'b0), .in5(1'b0), .in6(1'b0), .in7(1'b0),
    .in8(1'b0), .in9(1'b0), .in10(1'b0), .in11(1'b0), .in12(1'b0), .in13(1'b0), .in14(1'b0), .in15(1'b0),
    .out(OF), .sel(ALU_OP_021));

  // Notes on the sheet:
  //   X_IN
  //   Y_IN
  //   Y补码
  //   Y_IN
  //   X补码
  //   比较器
  //   与运算
  //   或运算
  //   异或运算
  //   逻辑左移
  //   逻辑右移
  //   算术右移
  //   无符号加法
  //   无符号减法
  //   有符号数加法溢出位检测
  //   有符号数减法溢出位检测
endmodule

module \_32位扩展器黄浩链  (
  input  [15:0] D_lin,
  input  D_sel_Huang,
  output [31:0] out_3
);

  wire [31:0] bit_extender_1_out, bit_extender_2_out;

  assign bit_extender_1_out = {{16{1'b0}}, D_lin};  // Bit_Extender bit_extender_1
  assign bit_extender_2_out = {{16{1'b0}}, D_lin};  // Bit_Extender bit_extender_2
  Multiplexer #(.select(1), .width(32), .disabled("Z"), .enable("false")) multiplexer_1 (
    .in0(bit_extender_1_out), .in1(bit_extender_2_out), .out(out_3), .sel(D_sel_Huang));

  // Notes on the sheet:
  //   0扩展
  //   符号扩展
endmodule

module CU_HUANG021 (
  input  in_1,
  input  in_2,
  input  in_3,
  input  in_4,
  input  [5:0] in_5,
  input  [5:0] in_6,
  output [23:0] out_7,
  output [1:0] rd_rt_sel,
  output [1:0] ALU_Y_sel,
  output [1:0] GR_D_sel,
  output [2:0] PC_D_SEL,
  output [3:0] ALU_OP
);

  wire ADD_HUANG021, ADDI_HUANG021, and_1_out, and_2_out, and_3_out, and_4_out, and_5_out, BEQ_HUANG021,
       M2_HUANG021, M4_HUANG021, not_1_out, not_2_out, or_1_out, or_2_out, or_5_out, rd_rt_sel_HUANG021,
       SKIP_HUANG021, SW_HUANG021;

  not not_1 (not_1_out, in_2);
  not not_2 (not_2_out, in_2);
  or or_1 (or_1_out, ADD_HUANG021, SW_HUANG021, ADDI_HUANG021);
  and and_1 (and_1_out, not_1_out, ADD_HUANG021);
  and and_2 (and_2_out, not_2_out, ADDI_HUANG021);
  \指令译码逻辑_黄浩链021  \u_指令译码逻辑_黄浩链021_1  (
    .OP(in_5), .Funct(in_6), .ADD(ADD_HUANG021), .SW(SW_HUANG021), .BEQ(BEQ_HUANG021), .ADDI(ADDI_HUANG021));
  and and_3 (and_3_out, BEQ_HUANG021, M2_HUANG021);
  and and_4 (and_4_out, ALU_OP[0], or_1_out);
  and and_5 (and_5_out, ADD_HUANG021, M4_HUANG021);
  and and_6 (out_7[0], SW_HUANG021, M4_HUANG021);
  or or_2 (or_2_out, and_1_out, and_2_out);
  \时序发生器_7状态_main  main_1 (
    .En(in_3), .skip(SKIP_HUANG021), .clk(in_4), .M1(out_7[7]), .M2(M2_HUANG021), .M4(M4_HUANG021),
    .M3(ALU_OP[0]));  // open: M0, clr, M7, M6, M5
  and and_7 (ALU_OP[1], ALU_OP[0], BEQ_HUANG021);
  or or_3 (out_7[6], out_7[7], and_3_out, and_4_out);
  or or_4 (rd_rt_sel_HUANG021, out_7[7], and_5_out);
  or or_5 (or_5_out, out_7[7], M4_HUANG021);
  or or_6 (out_7[4], BEQ_HUANG021, ADD_HUANG021, SW_HUANG021, ADDI_HUANG021);
  and and_8 (out_7[8], or_2_out, M4_HUANG021);
  and and_9 (out_7[1], or_5_out, SW_HUANG021);

  assign ALU_OP[3:2] = 2'b00;
  assign ALU_Y_sel[0] = ALU_Y_sel[1];
  assign out_7[2] = out_7[7];

  // Other names for the same wires on the sheet: ALU_OP_0 = ALU_OP[0]; M3_HUANG021 = ALU_OP[0]; ALU_OP_1 = ALU_OP[1];
  //   ALU_Y_sel_0 = ALU_Y_sel[1]; CLK = in_4; EN = in_3; FUNCT[5:0] = in_6; GR_D_s_HUANG021_0 = GR_D_sel[0];
  //   GR_D_s_HUANG_021_1 = GR_D_sel[1]; OF = in_2; OP[5:0] = in_5; RAM_Addr_s_HUANG021 = out_7[0];
  //   W_RAM_HUANG021 = out_7[1]; W_IR_HUANG021 = out_7[3]; ALU_X_sel = out_7[4]; S_Extend = out_7[5];
  //   W_F_HUANG021 = out_7[6]; M1_HUANG021 = out_7[7]; R_MEN_HUANG021 = out_7[7]; W_PC_HUANG021 = out_7[7];
  //   W_GR_HUANG021 = out_7[8]; PC_D_SEL_HUANG021_0 = PC_D_SEL[0]; PC_D_SEL_HUANG_021_1 = PC_D_SEL[1];
  //   PC_D_SEL_HUANG_021_2 = PC_D_SEL[2]; rd_rt_sel_HUANG021_0 = rd_rt_sel[0]; rd_rt_sel_HUANG_021_1 = rd_rt_sel[1];
  //   ZF = in_1
endmodule

module \指令译码逻辑_黄浩链021  (
  input  [5:0] OP,
  input  [5:0] Funct,
  output BEQ,
  output ADD,
  output SW,
  output ADDI
);

  wire nor_1_out, not_1_out, not_2_out, not_3_out, not_4_out, R;

  not not_1 (not_1_out, OP[4]);
  not not_2 (not_2_out, OP[2]);
  and and_1 (SW, OP[5], not_1_out, OP[3], not_2_out, OP[1], OP[0]);
  nor nor_1 (nor_1_out, Funct[0], Funct[1], Funct[2], Funct[3], Funct[4]);
  and and_2 (ADD, nor_1_out, Funct[5], R);
  nor nor_2 (R, OP[0], OP[1], OP[2], OP[3], OP[4], OP[5]);
  not not_3 (not_3_out, OP[2]);
  not not_4 (not_4_out, OP[3]);
  nor nor_3 (BEQ, OP[5], OP[4], OP[3], not_3_out, OP[1], OP[0]);
  nor nor_4 (ADDI, OP[5], OP[4], not_4_out, OP[2], OP[1], OP[0]);

  // Other names for the same wires on the sheet: I0 = Funct[0]; I1 = Funct[1]; I2 = Funct[2]; I3 = Funct[3];
  //   I4 = Funct[4]; I5 = Funct[5]; I26 = OP[0]; I27 = OP[1]; I28 = OP[2]; I29 = OP[3]; I30 = OP[4]; I31 = OP[5]
endmodule
